// Logisim project ej4.c.circ as structural Verilog: 3 circuits, main circuit main
module main (
  input  [3:0] a,
  input  cin,
  input  [3:0] b,
  output [3:0] S,
  output Cout
);

  wire suma_1_c, suma_2_c, suma_4_c;

  suma suma_1 (.a(a[0]), .b(b[0]), .Cin(cin), .S(S[0]), .C(suma_1_c));
  suma suma_2 (.a(a[2]), .b(b[2]), .Cin(suma_4_c), .S(S[2]), .C(suma_2_c));
  suma suma_3 (.a(a[3]), .b(b[3]), .Cin(suma_2_c), .S(S[3]), .C(Cout));
  suma suma_4 (.a(a[1]), .b(b[1]), .Cin(suma_1_c), .S(S[1]), .C(suma_4_c));
endmodule

module suma (
  input  a,
  input  b,
  input  Cin,
  output S,
  output C
);

  wire and_1_out, and_2_out, xor_1_out;

  and and_1 (and_1_out, a, b);
  xor xor_1 (xor_1_out, a, b);
  or or_1 (C, and_1_out, and_2_out);
  and and_2 (and_2_out, xor_1_out, Cin);
  xor xor_2 (S, Cin, xor_1_out);

  // Notes on the sheet:
  //   a: pull=down
endmodule

module sumaSinAcarreo (
  input  a,
  input  b,
  output S,
  output C
);

  and and_1 (C, a, b);
  xor xor_1 (S, a, b);

  // Notes on the sheet:
  //   a: pull=down
endmodule
