// Logisim project ej4.d.circ as structural Verilog: 1 circuit, main circuit main
module main (
  input  [3:0] in_1,
  output out_2
);

  wire or_1_out, or_2_out, or_3_out;

  or or_1 (or_1_out, in_1[0], in_1[1]);
  or or_2 (or_2_out, in_1[2], in_1[3]);
  or or_3 (or_3_out, or_1_out, or_2_out);
  not not_1 (out_2, or_3_out);
endmodule
