// Logisim project ej4.e.circ as structural Verilog: 4 circuits, main circuit main
module main (
  input  [3:0] a,
  input  [3:0] b,
  input  cin,
  output Z,
  output V,
  output N,
  output C
);

  wire and_1_out, and_2_out, and_3_out, not_1_out, not_2_out, or_1_out, or_2_out, or_3_out, xor_1_out;
  wire [2:0] suma4bits_1_s;

  xor xor_1 (xor_1_out, b[3], a[3]);
  and and_1 (and_1_out, b[3], a[3]);
  or or_1 (or_1_out, b[3], a[3]);
  not not_1 (not_1_out, or_1_out);
  suma4bits suma4bits_1 (.a(a), .b(b), .cin(cin), .S({N, suma4bits_1_s}), .Cout(C));
  ComparadorconCero comparadorconcero_1 (.in_1({N, suma4bits_1_s}), .out_2(Z));
  not not_2 (not_2_out, N);
  and and_2 (and_2_out, and_1_out, N);
  and and_3 (and_3_out, not_1_out, not_2_out);
  or or_2 (or_2_out, and_3_out, and_2_out);
  or or_3 (or_3_out, xor_1_out, or_2_out);
  not not_3 (V, or_3_out);
endmodule

module suma (
  input  a,
  input  b,
  input  Cin,
  output S,
  output C
);

  wire and_1_out, and_2_out, xor_1_out;

  and and_1 (and_1_out, a, b);
  xor xor_1 (xor_1_out, a, b);
  or or_1 (C, and_1_out, and_2_out);
  and and_2 (and_2_out, xor_1_out, Cin);
  xor xor_2 (S, Cin, xor_1_out);

  // Notes on the sheet:
  //   a: pull=down
endmodule

module suma4bits (
  input  [3:0] a,
  input  [3:0] b,
  input  cin,
  output [3:0] S,
  output Cout
);

  wire suma_1_c, suma_2_c, suma_4_c;

  suma suma_1 (.a(a[0]), .b(b[0]), .Cin(cin), .S(S[0]), .C(suma_1_c));
  suma suma_2 (.a(a[2]), .b(b[2]), .Cin(suma_4_c), .S(S[2]), .C(suma_2_c));
  suma suma_3 (.a(a[3]), .b(b[3]), .Cin(suma_2_c), .S(S[3]), .C(Cout));
  suma suma_4 (.a(a[1]), .b(b[1]), .Cin(suma_1_c), .S(S[1]), .C(suma_4_c));
endmodule

module ComparadorconCero (
  input  [3:0] in_1,
  output out_2
);

  wire or_1_out, or_2_out, or_3_out;

  or or_1 (or_1_out, in_1[0], in_1[1]);
  or or_2 (or_2_out, in_1[2], in_1[3]);
  or or_3 (or_3_out, or_1_out, or_2_out);
  not not_1 (out_2, or_3_out);
endmodule
