// Logisim project ej4.a.circ as structural Verilog: 1 circuit, main circuit main
module main (
  input  a,
  input  b,
  output C,
  output S
);

  and and_1 (C, a, b);
  xor xor_1 (S, a, b);

  // Notes on the sheet:
  //   a: pull=down
  //   EJ 4.a:
  //   EJ 4.b
endmodule
