// Logisim project TallerLogica-Secuenciales.circ as structural Verilog
module buffer_tres_estados (
  input  A,
  input  A_en,
  input  B,
  input  B_en,
  input  C,
  input  C_en,
  output Res
);

  assign Res = A_en ? A : 1'bz;  // Controlled_Buffer controlled_buffer_1
  assign Res = B_en ? B : 1'bz;  // Controlled_Buffer controlled_buffer_2
  assign Res = C_en ? C : 1'bz;  // Controlled_Buffer controlled_buffer_3
endmodule

module registro_salida_restringida (
  input  clk,
  input  Reg_in,
  input  w,
  input  en_out,
  output Reg_Debug,
  output Reg_output
);

  wire and_1_out, d_ff_1_q, not_1_out;

  D_Flip_Flop d_ff_1 (.D(w), .clk(clk), .Q(d_ff_1_q), .reset(and_1_out));  // open: Qn, preset
  not not_1 (not_1_out, clk);
  and and_1 (and_1_out, not_1_out, d_ff_1_q);
  D_Flip_Flop d_ff_2 (.D(Reg_in), .clk(d_ff_1_q), .Q(Reg_Debug));  // open: Qn, preset, reset
  assign Reg_output = en_out ? Reg_Debug : 1'bz;  // Controlled_Buffer controlled_buffer_1
endmodule

module registro_4bytes_salida (
  input  [3:0] Reg4_in,
  input  clk,
  input  w,
  input  en_out,
  output [3:0] Reg4_Debug,
  output [3:0] Reg4_output
);

  registro_salida_restringida registro_salida_restringida_1 (
    .clk(clk), .Reg_in(Reg4_in[0]), .w(w), .en_out(en_out), .Reg_Debug(Reg4_Debug[0]),
    .Reg_output(Reg4_output[0]));
  registro_salida_restringida registro_salida_restringida_2 (
    .clk(clk), .Reg_in(Reg4_in[1]), .w(w), .en_out(en_out), .Reg_Debug(Reg4_Debug[1]),
    .Reg_output(Reg4_output[1]));
  registro_salida_restringida registro_salida_restringida_3 (
    .clk(clk), .Reg_in(Reg4_in[2]), .w(w), .en_out(en_out), .Reg_Debug(Reg4_Debug[2]),
    .Reg_output(Reg4_output[2]));
  registro_salida_restringida registro_salida_restringida_4 (
    .clk(clk), .Reg_in(Reg4_in[3]), .w(w), .en_out(en_out), .Reg_Debug(Reg4_Debug[3]),
    .Reg_output(Reg4_output[3]));

  // Other names for the same wires on the sheet: en = en_out
endmodule

module ALU_regs (
  input  clk,
  input  [3:0] A,
  input  A_Write,
  input  [3:0] B,
  input  B_Write,
  input  in_6,
  input  [1:0] OP,
  output [3:0] A_Debug,
  output [3:0] B_Debug,
  output Z,
  output N,
  output V,
  output C,
  output [3:0] S_Debug,
  output [3:0] Reg4_output
);

  wire not_1_out;
  wire [3:0] alu_1_out_4, registro_4bytes_salida_1_reg4_output, registro_4bytes_salida_2_reg4_output;

  Hex_Digit_Display hex_digit_display_1 (.value(A_Debug));  // open: dp
  registro_4bytes_salida registro_4bytes_salida_1 (
    .Reg4_in(A), .clk(clk), .w(A_Write), .en_out(1'b1), .Reg4_Debug(A_Debug),
    .Reg4_output(registro_4bytes_salida_1_reg4_output));
  registro_4bytes_salida registro_4bytes_salida_2 (
    .Reg4_in(B), .clk(clk), .w(B_Write), .en_out(1'b1), .Reg4_Debug(B_Debug),
    .Reg4_output(registro_4bytes_salida_2_reg4_output));
  Hex_Digit_Display hex_digit_display_2 (.value(B_Debug));  // open: dp
  ALU alu_1 (
    .A(registro_4bytes_salida_1_reg4_output), .B(registro_4bytes_salida_2_reg4_output), .OP(OP),
    .out_4(alu_1_out_4), .Z(Z), .N(N), .V(V), .C(C));
  not not_1 (not_1_out, clk);
  registro_4bytes_salida registro_4bytes_salida_3 (
    .Reg4_in(alu_1_out_4), .clk(not_1_out), .w(1'b1), .en_out(in_6), .Reg4_Debug(S_Debug),
    .Reg4_output(Reg4_output));
  Hex_Digit_Display hex_digit_display_3 (.value(S_Debug));  // open: dp
endmodule

module ej_02 (
  input  in_1,
  input  in_2,
  input  in_3,
  input  in_4,
  input  clk,
  input  Force_Input,
  input  in_7,
  input  in_8,
  input  en_Force_Input,
  output R0,
  output out_11,
  output R1,
  output R2
);

  assign out_11 = en_Force_Input ? Force_Input : 1'bz;  // Controlled_Buffer controlled_buffer_1
  registro_salida_restringida registro_salida_restringida_1 (
    .clk(clk), .Reg_in(out_11), .w(in_1), .en_out(in_2), .Reg_Debug(R0), .Reg_output(out_11));
  registro_salida_restringida registro_salida_restringida_2 (
    .clk(clk), .Reg_in(out_11), .w(in_3), .en_out(in_4), .Reg_Debug(R1), .Reg_output(out_11));
  registro_salida_restringida registro_salida_restringida_3 (
    .clk(clk), .Reg_in(out_11), .w(in_7), .en_out(in_8), .Reg_Debug(R2), .Reg_output(out_11));
endmodule

module ej_03 (
  input  clk,
  input  ALU_A_Write,
  input  ALU_B_Write,
  input  [1:0] OP,
  input  ALU_enableOut,
  input  Reg0_Write,
  input  Reg0_enableOut,
  input  Reg1_Write,
  input  Reg1_enableOut,
  input  Reg2_Write,
  input  Reg2_enableOut,
  input  Reg3_Write,
  input  Reg3_enableOut,
  input  [3:0] Force_Input,
  input  en_Force_Input,
  output N,
  output Z,
  output V,
  output C
);

  wire [3:0] alu_regs_1_a_debug, alu_regs_1_b_debug, alu_regs_1_s_debug, controlled_buffer_1_out,
       Registro_00_reg4_debug, Registro_00_reg4_output, Registro_01_reg4_debug, Registro_02_reg4_debug,
       Registro_03_reg4_debug;

  assign controlled_buffer_1_out = en_Force_Input ? Force_Input : 4'bz;  // Controlled_Buffer controlled_buffer_1
  registro_4bytes_salida Registro_00 (
    .Reg4_in(controlled_buffer_1_out), .clk(clk), .w(Reg0_Write), .en_out(Reg0_enableOut),
    .Reg4_Debug(Registro_00_reg4_debug), .Reg4_output(Registro_00_reg4_output));
  registro_4bytes_salida Registro_01 (
    .Reg4_in(controlled_buffer_1_out), .clk(clk), .w(Reg1_Write), .en_out(Reg1_enableOut),
    .Reg4_Debug(Registro_01_reg4_debug), .Reg4_output(Registro_00_reg4_output));
  registro_4bytes_salida Registro_02 (
    .Reg4_in(controlled_buffer_1_out), .clk(clk), .w(Reg2_Write), .en_out(Reg2_enableOut),
    .Reg4_Debug(Registro_02_reg4_debug), .Reg4_output(Registro_00_reg4_output));
  registro_4bytes_salida Registro_03 (
    .Reg4_in(controlled_buffer_1_out), .clk(clk), .w(Reg3_Write), .en_out(Reg3_enableOut),
    .Reg4_Debug(Registro_03_reg4_debug), .Reg4_output(Registro_00_reg4_output));
  Hex_Digit_Display hex_digit_display_1 (.value(Registro_00_reg4_debug));  // open: dp
  Hex_Digit_Display hex_digit_display_2 (.value(Registro_01_reg4_debug));  // open: dp
  Hex_Digit_Display hex_digit_display_3 (.value(Registro_02_reg4_debug));  // open: dp
  Hex_Digit_Display hex_digit_display_4 (.value(Registro_03_reg4_debug));  // open: dp
  Hex_Digit_Display hex_digit_display_5 (.value(alu_regs_1_a_debug));  // open: dp
  Hex_Digit_Display Bus_2 (.value(controlled_buffer_1_out));  // open: dp
  Hex_Digit_Display hex_digit_display_6 (.value(alu_regs_1_b_debug));  // open: dp
  ALU_regs alu_regs_1 (
    .in_6(ALU_enableOut), .A(Registro_00_reg4_output), .A_Write(ALU_A_Write), .B(Registro_00_reg4_output),
    .B_Write(ALU_B_Write), .clk(clk), .OP(OP), .S_Debug(alu_regs_1_s_debug),
    .Reg4_output(controlled_buffer_1_out), .A_Debug(alu_regs_1_a_debug), .B_Debug(alu_regs_1_b_debug), .Z(Z),
    .N(N), .V(V), .C(C));
  Hex_Digit_Display hex_digit_display_7 (.value(alu_regs_1_s_debug));  // open: dp
endmodule

module sumador_simple (
  input  A,
  input  B,
  output S,
  output Cout
);

  xor xor_1 (S, A, B);
  and and_1 (Cout, A, B);
endmodule

module sumador_completo (
  input  Cin,
  input  A,
  input  B,
  output S,
  output Cout
);

  wire sumador_simple_1_cout, sumador_simple_1_s, sumador_simple_2_cout;

  sumador_simple sumador_simple_1 (.A(A), .B(B), .S(sumador_simple_1_s), .Cout(sumador_simple_1_cout));
  sumador_simple sumador_simple_2 (.A(Cin), .B(sumador_simple_1_s), .S(S), .Cout(sumador_simple_2_cout));
  or or_1 (Cout, sumador_simple_2_cout, sumador_simple_1_cout);
endmodule

module sumador_4 (
  input  Cin,
  input  [3:0] A,
  input  [3:0] B,
  output [3:0] S,
  output Cout
);

  wire sumador_completo_1_cout, sumador_completo_2_cout, sumador_completo_3_cout;

  sumador_completo sumador_completo_1 (.Cin(Cin), .A(A[0]), .B(B[0]), .S(S[0]), .Cout(sumador_completo_1_cout));
  sumador_completo sumador_completo_2 (
    .Cin(sumador_completo_1_cout), .A(A[1]), .B(B[1]), .S(S[1]), .Cout(sumador_completo_2_cout));
  sumador_completo sumador_completo_3 (
    .Cin(sumador_completo_2_cout), .A(A[2]), .B(B[2]), .S(S[2]), .Cout(sumador_completo_3_cout));
  sumador_completo sumador_completo_4 (.Cin(sumador_completo_3_cout), .A(A[3]), .B(B[3]), .S(S[3]), .Cout(Cout));
  Hex_Digit_Display hex_digit_display_1 (.value(S));  // open: dp
endmodule

module comparador_cero (
  input  [3:0] A,
  output Z
);

  wire or_1_out, or_2_out, or_3_out;

  or or_1 (or_1_out, A[0], A[1]);
  or or_2 (or_2_out, A[2], A[3]);
  or or_3 (or_3_out, or_1_out, or_2_out);
  not not_1 (Z, or_3_out);
endmodule

module sumador_flags (
  input  cin,
  input  [3:0] a,
  input  [3:0] b,
  output [3:0] S,
  output Z,
  output V,
  output N,
  output C
);

  wire not_1_out, xor_1_out, xor_2_out;

  xor xor_1 (xor_1_out, b[3], a[3]);
  not not_1 (not_1_out, xor_1_out);
  sumador_4 sumador_4_1 (.Cin(cin), .A(a), .B(b), .S({N, S[2:0]}), .Cout(C));
  comparador_cero comparador_cero_1 (.A({N, S[2:0]}), .Z(Z));
  xor xor_2 (xor_2_out, a[3], N);
  and and_1 (V, not_1_out, xor_2_out);

  assign S[3] = N;
endmodule

module incrementador_4 (
  input  [3:0] A,
  output [3:0] S
);

  sumador_4 sumador_4_1 (.A(A), .B(4'b0001), .S(S));  // open: Cin, Cout
  Hex_Digit_Display hex_digit_display_1 (.value(S));  // open: dp
endmodule

module inversor_4 (
  input  [3:0] A,
  input  INV,
  output [3:0] S
);

  wire [3:0] not_1_out;

  assign not_1_out = ~A;  // NOT_Gate not_1, 4 bits wide
  Multiplexer #(.width(4)) multiplexer_1 (.in0(A), .in1(not_1_out), .out(S), .sel(INV));
  Hex_Digit_Display hex_digit_display_1 (.value(S));  // open: dp
endmodule

module ALU (
  input  [3:0] A,
  input  [3:0] B,
  input  [1:0] OP,
  output [3:0] out_4,
  output Z,
  output N,
  output V,
  output C
);

  wire comparador_cero_1_z, comprobador_v_1_v, multiplexer_5_out, not_1_out, or_1_out, sumador_4_1_cout;
  wire [3:0] and_4_1_s, incrementador_4_1_s, inversor_4_1_s, multiplexer_2_out, multiplexer_3_out,
       multiplexer_4_out, or_4_1_s, sumador_4_1_s;

  comprobador_V comprobador_v_1 (.resta(OP[0]), .a(A), .b(B), .V(comprobador_v_1_v));
  inversor_4 inversor_4_1 (.A(B), .INV(OP[0]), .S(inversor_4_1_s));
  Multiplexer multiplexer_1 (.in0(comprobador_v_1_v), .in1(1'b0), .out(V), .sel(OP[1]));
  AND_4 and_4_1 (.A(A), .B(B), .S(and_4_1_s));
  OR_4 or_4_1 (.A(A), .B(B), .S(or_4_1_s));
  incrementador_4 incrementador_4_1 (.A(inversor_4_1_s), .S(incrementador_4_1_s));
  Multiplexer #(.width(4)) multiplexer_2 (.in0(and_4_1_s), .in1(or_4_1_s), .out(multiplexer_2_out), .sel(OP[0]));
  Multiplexer #(.width(4)) multiplexer_3 (
    .in0(inversor_4_1_s), .in1(incrementador_4_1_s), .out(multiplexer_3_out), .sel(OP[0]));
  Hex_Digit_Display hex_digit_display_1 (.value(multiplexer_3_out));  // open: dp
  sumador_4 sumador_4_1 (.A(A), .B(multiplexer_3_out), .S(sumador_4_1_s), .Cout(sumador_4_1_cout));  // open: Cin
  Multiplexer #(.width(4)) multiplexer_4 (
    .in0(sumador_4_1_s), .in1(multiplexer_2_out), .out(multiplexer_4_out), .sel(OP[1]));
  Multiplexer multiplexer_5 (.in0(sumador_4_1_cout), .in1(not_1_out), .out(multiplexer_5_out), .sel(OP[0]));
  not not_1 (not_1_out, sumador_4_1_cout);
  comparador_cero comparador_cero_1 (.A(B), .Z(comparador_cero_1_z));
  sumador_flags sumador_flags_1 (.a(multiplexer_4_out), .S(out_4), .Z(Z), .N(N));  // open: cin, b, V, C
  Multiplexer multiplexer_6 (.in0(multiplexer_5_out), .in1(1'b0), .out(C), .sel(or_1_out));
  or or_1 (or_1_out, OP[1], comparador_cero_1_z);
  Hex_Digit_Display hex_digit_display_2 (.value(out_4));  // open: dp
endmodule

module verificador (
  output [3:0] out_1,
  output [3:0] out_2,
  output [1:0] out_3,
  output halt,
  output N,
  output Z,
  output V,
  output C,
  output [3:0] res
);

  wire clock_1_out;

  Clock clock_1 (.out(clock_1_out));
  Counter #(.max('h3ff), .width(10)) counter_1 (
    .clk(clock_1_out), .carry(halt), .Q({out_3, out_2, out_1}));  // open: clr, load, up, count, D
  // ALU alu_1: pin names not known; wires that end beside it: out_1, out_2, out_3, N, Z, V, C, res
endmodule

module Flags (
  input  cin,
  input  [3:0] a,
  input  [3:0] b,
  output Z,
  output V,
  output N,
  output C
);

  wire and_1_out, and_2_out, and_3_out, not_1_out, not_2_out, or_1_out, or_2_out, or_3_out, xor_1_out;
  wire [2:0] sumador_4_1_s;

  xor xor_1 (xor_1_out, b[3], a[3]);
  and and_1 (and_1_out, b[3], a[3]);
  or or_1 (or_1_out, b[3], a[3]);
  not not_1 (not_1_out, or_1_out);
  sumador_4 sumador_4_1 (.Cin(cin), .A(a), .B(b), .S({N, sumador_4_1_s}), .Cout(C));
  comparador_cero comparador_cero_1 (.A({N, sumador_4_1_s}), .Z(Z));
  not not_2 (not_2_out, N);
  and and_2 (and_2_out, and_1_out, N);
  and and_3 (and_3_out, not_1_out, not_2_out);
  or or_2 (or_2_out, and_3_out, and_2_out);
  or or_3 (or_3_out, xor_1_out, or_2_out);
  not not_3 (V, or_3_out);
endmodule

module AND_4 (
  input  [3:0] A,
  input  [3:0] B,
  output [3:0] S
);

  and and_1 (S[0], A[0], B[0]);
  and and_2 (S[1], A[1], B[1]);
  and and_3 (S[2], A[2], B[2]);
  and and_4 (S[3], A[3], B[3]);
endmodule

module OR_4 (
  input  [3:0] A,
  input  [3:0] B,
  output [3:0] S
);

  or or_1 (S[0], A[0], B[0]);
  or or_2 (S[1], A[1], B[1]);
  or or_3 (S[2], A[2], B[2]);
  or or_4 (S[3], A[3], B[3]);
endmodule

module prueba (
  input  [3:0] A,
  input  [3:0] B,
  input  [1:0] OP,
  output [3:0] S,
  output Z,
  output V,
  output N,
  output C
);

  wire multiplexer_4_out, not_1_out, not_2_out, sumador_flags_1_c, sumador_flags_1_v;
  wire [3:0] and_4_1_s, incrementador_4_1_s, inversor_4_1_s, multiplexer_1_out, multiplexer_2_out, or_4_1_s,
       sumador_flags_1_s;

  inversor_4 inversor_4_1 (.A(B), .INV(OP[0]), .S(inversor_4_1_s));
  AND_4 and_4_1 (.A(A), .B(B), .S(and_4_1_s));
  OR_4 or_4_1 (.A(A), .B(B), .S(or_4_1_s));
  incrementador_4 incrementador_4_1 (.A(inversor_4_1_s), .S(incrementador_4_1_s));
  Multiplexer #(.width(4)) multiplexer_1 (.in0(and_4_1_s), .in1(or_4_1_s), .out(multiplexer_1_out), .sel(OP[0]));
  Multiplexer #(.width(4)) multiplexer_2 (
    .in0(inversor_4_1_s), .in1(incrementador_4_1_s), .out(multiplexer_2_out), .sel(OP[0]));
  Hex_Digit_Display hex_digit_display_1 (.value(multiplexer_2_out));  // open: dp
  sumador_flags sumador_flags_1 (
    .a(A), .b(multiplexer_2_out), .S(sumador_flags_1_s), .V(sumador_flags_1_v), .N(N), .C(sumador_flags_1_c));  // open: cin, Z
  Multiplexer #(.width(4)) multiplexer_3 (.in0(multiplexer_1_out), .in1(sumador_flags_1_s), .out(S), .sel(not_1_out));
  not not_1 (not_1_out, OP[0]);
  not not_2 (not_2_out, sumador_flags_1_c);
  Multiplexer multiplexer_4 (.in0(sumador_flags_1_c), .in1(not_2_out), .out(multiplexer_4_out), .sel(OP[0]));
  Multiplexer multiplexer_5 (.in0(sumador_flags_1_v), .in1(1'b0), .out(V), .sel(OP[1]));
  Multiplexer multiplexer_6 (.in0(multiplexer_4_out), .in1(1'b0), .out(C), .sel(OP[1]));
  Hex_Digit_Display hex_digit_display_2 (.value(S));  // open: dp
  comparador_cero comparador_cero_1 (.A(S), .Z(Z));
endmodule

module comprobador_V (
  input  resta,
  input  [3:0] a,
  input  [3:0] b,
  output V
);

  wire multiplexer_2_out, not_1_out, xor_1_out, xor_2_out;
  wire [3:0] incrementador_4_1_s, inversor_4_1_s, multiplexer_1_out, sumador_4_1_s;

  inversor_4 inversor_4_1 (.A(b), .INV(resta), .S(inversor_4_1_s));
  incrementador_4 incrementador_4_1 (.A(inversor_4_1_s), .S(incrementador_4_1_s));
  xor xor_1 (xor_1_out, b[3], a[3]);
  Multiplexer #(.width(4)) multiplexer_1 (
    .in0(inversor_4_1_s), .in1(incrementador_4_1_s), .out(multiplexer_1_out), .sel(resta));
  sumador_4 sumador_4_1 (.A(a), .B(multiplexer_1_out), .S(sumador_4_1_s));  // open: Cin, Cout
  not not_1 (not_1_out, xor_1_out);
  Multiplexer multiplexer_2 (.in0(not_1_out), .in1(xor_1_out), .out(multiplexer_2_out), .sel(resta));
  xor xor_2 (xor_2_out, a[3], sumador_4_1_s[3]);
  and and_1 (V, multiplexer_2_out, xor_2_out);
endmodule
