// Logisim project ej4completo.circ as structural Verilog
module sumador_simple (
  input  A,
  input  B,
  output S,
  output Cout
);

  xor xor_1 (S, A, B);
  and and_1 (Cout, A, B);
endmodule

module sumador_completo (
  input  Cin,
  input  A,
  input  B,
  output S,
  output Cout
);

  wire sumador_simple_1_cout, sumador_simple_1_s, sumador_simple_2_cout;

  sumador_simple sumador_simple_1 (.A(A), .B(B), .S(sumador_simple_1_s), .Cout(sumador_simple_1_cout));
  sumador_simple sumador_simple_2 (.A(Cin), .B(sumador_simple_1_s), .S(S), .Cout(sumador_simple_2_cout));
  or or_1 (Cout, sumador_simple_2_cout, sumador_simple_1_cout);
endmodule

module sumador_4 (
  input  Cin,
  input  [3:0] A,
  input  [3:0] B,
  output [3:0] S,
  output Cout
);

  wire sumador_completo_1_cout, sumador_completo_2_cout, sumador_completo_3_cout;

  sumador_completo sumador_completo_1 (.Cin(Cin), .A(A[0]), .B(B[0]), .S(S[0]), .Cout(sumador_completo_1_cout));
  sumador_completo sumador_completo_2 (
    .Cin(sumador_completo_1_cout), .A(A[1]), .B(B[1]), .S(S[1]), .Cout(sumador_completo_2_cout));
  sumador_completo sumador_completo_3 (
    .Cin(sumador_completo_2_cout), .A(A[2]), .B(B[2]), .S(S[2]), .Cout(sumador_completo_3_cout));
  sumador_completo sumador_completo_4 (.Cin(sumador_completo_3_cout), .A(A[3]), .B(B[3]), .S(S[3]), .Cout(Cout));
  Hex_Digit_Display hex_digit_display_1 (.value(S));  // open: dp
endmodule

module comparador_cero (
  input  [3:0] A,
  output Z
);

  wire or_1_out, or_2_out, or_3_out;

  or or_1 (or_1_out, A[0], A[1]);
  or or_2 (or_2_out, A[2], A[3]);
  or or_3 (or_3_out, or_1_out, or_2_out);
  not not_1 (Z, or_3_out);
endmodule

module sumador_flags (
  input  cin,
  input  [3:0] a,
  input  [3:0] b,
  output [3:0] S,
  output Z,
  output V,
  output N,
  output C
);

  wire not_1_out, xor_1_out, xor_2_out;

  xor xor_1 (xor_1_out, b[3], a[3]);
  not not_1 (not_1_out, xor_1_out);
  sumador_4 sumador_4_1 (.Cin(cin), .A(a), .B(b), .S({N, S[2:0]}), .Cout(C));
  comparador_cero comparador_cero_1 (.A({N, S[2:0]}), .Z(Z));
  xor xor_2 (xor_2_out, a[3], N);
  and and_1 (V, not_1_out, xor_2_out);

  assign S[3] = N;
endmodule

module incrementador_4 (
  input  [3:0] A,
  output [3:0] S
);

  sumador_4 sumador_4_1 (.A(A), .B(4'b0001), .S(S));  // open: Cin, Cout
  Hex_Digit_Display hex_digit_display_1 (.value(S));  // open: dp
endmodule

module inversor_4 (
  input  [3:0] A,
  input  INV,
  output [3:0] S
);

  wire [3:0] not_1_out;

  assign not_1_out = ~A;  // NOT_Gate not_1, 4 bits wide
  Multiplexer #(.width(4)) multiplexer_1 (.in0(A), .in1(not_1_out), .out(S), .sel(INV));
  Hex_Digit_Display hex_digit_display_1 (.value(S));  // open: dp
endmodule

module ALU (
  input  [3:0] A,
  input  [3:0] B,
  input  [1:0] OP,
  output [3:0] out_4,
  output Z,
  output N,
  output V,
  output C
);

  wire comparador_cero_1_z, comprobador_v_1_v, multiplexer_5_out, not_1_out, or_1_out, sumador_4_1_cout;
  wire [3:0] and_4_1_s, incrementador_4_1_s, inversor_4_1_s, multiplexer_2_out, multiplexer_3_out,
       multiplexer_4_out, or_4_1_s, sumador_4_1_s;

  comprobador_V comprobador_v_1 (.resta(OP[0]), .a(A), .b(B), .V(comprobador_v_1_v));
  inversor_4 inversor_4_1 (.A(B), .INV(OP[0]), .S(inversor_4_1_s));
  Multiplexer multiplexer_1 (.in0(comprobador_v_1_v), .in1(1'b0), .out(V), .sel(OP[1]));
  AND_4 and_4_1 (.A(A), .B(B), .S(and_4_1_s));
  OR_4 or_4_1 (.A(A), .B(B), .S(or_4_1_s));
  incrementador_4 incrementador_4_1 (.A(inversor_4_1_s), .S(incrementador_4_1_s));
  Multiplexer #(.width(4)) multiplexer_2 (.in0(and_4_1_s), .in1(or_4_1_s), .out(multiplexer_2_out), .sel(OP[0]));
  Multiplexer #(.width(4)) multiplexer_3 (
    .in0(inversor_4_1_s), .in1(incrementador_4_1_s), .out(multiplexer_3_out), .sel(OP[0]));
  Hex_Digit_Display hex_digit_display_1 (.value(multiplexer_3_out));  // open: dp
  sumador_4 sumador_4_1 (.A(A), .B(multiplexer_3_out), .S(sumador_4_1_s), .Cout(sumador_4_1_cout));  // open: Cin
  Multiplexer #(.width(4)) multiplexer_4 (
    .in0(sumador_4_1_s), .in1(multiplexer_2_out), .out(multiplexer_4_out), .sel(OP[1]));
  Multiplexer multiplexer_5 (.in0(sumador_4_1_cout), .in1(not_1_out), .out(multiplexer_5_out), .sel(OP[0]));
  not not_1 (not_1_out, sumador_4_1_cout);
  comparador_cero comparador_cero_1 (.A(B), .Z(comparador_cero_1_z));
  sumador_flags sumador_flags_1 (.a(multiplexer_4_out), .S(out_4), .Z(Z), .N(N));  // open: cin, b, V, C
  Multiplexer multiplexer_6 (.in0(multiplexer_5_out), .in1(1'b0), .out(C), .sel(or_1_out));
  or or_1 (or_1_out, OP[1], comparador_cero_1_z);
  Hex_Digit_Display hex_digit_display_2 (.value(out_4));  // open: dp
endmodule

module verificador (
  output [3:0] out_1,
  output [3:0] out_2,
  output [1:0] out_3,
  output halt,
  output N,
  output Z,
  output V,
  output C,
  output [3:0] res
);

  wire clock_1_out;

  Clock clock_1 (.out(clock_1_out));
  Counter #(.max('h3ff), .width(10)) counter_1 (
    .clk(clock_1_out), .carry(halt), .Q({out_3, out_2, out_1}));  // open: clr, load, up, count, D
  // ALU alu_1: pin names not known; wires that end beside it: out_1, out_2, out_3, N, Z, V, C, res
endmodule

module Flags (
  input  cin,
  input  [3:0] a,
  input  [3:0] b,
  output Z,
  output V,
  output N,
  output C
);

  wire and_1_out, and_2_out, and_3_out, not_1_out, not_2_out, or_1_out, or_2_out, or_3_out, xor_1_out;
  wire [2:0] sumador_4_1_s;

  xor xor_1 (xor_1_out, b[3], a[3]);
  and and_1 (and_1_out, b[3], a[3]);
  or or_1 (or_1_out, b[3], a[3]);
  not not_1 (not_1_out, or_1_out);
  sumador_4 sumador_4_1 (.Cin(cin), .A(a), .B(b), .S({N, sumador_4_1_s}), .Cout(C));
  comparador_cero comparador_cero_1 (.A({N, sumador_4_1_s}), .Z(Z));
  not not_2 (not_2_out, N);
  and and_2 (and_2_out, and_1_out, N);
  and and_3 (and_3_out, not_1_out, not_2_out);
  or or_2 (or_2_out, and_3_out, and_2_out);
  or or_3 (or_3_out, xor_1_out, or_2_out);
  not not_3 (V, or_3_out);
endmodule

module AND_4 (
  input  [3:0] A,
  input  [3:0] B,
  output [3:0] S
);

  and and_1 (S[0], A[0], B[0]);
  and and_2 (S[1], A[1], B[1]);
  and and_3 (S[2], A[2], B[2]);
  and and_4 (S[3], A[3], B[3]);
endmodule

module OR_4 (
  input  [3:0] A,
  input  [3:0] B,
  output [3:0] S
);

  or or_1 (S[0], A[0], B[0]);
  or or_2 (S[1], A[1], B[1]);
  or or_3 (S[2], A[2], B[2]);
  or or_4 (S[3], A[3], B[3]);
endmodule

module prueba (
  input  [3:0] A,
  input  [3:0] B,
  input  [1:0] OP,
  output [3:0] S,
  output Z,
  output V,
  output N,
  output C
);

  wire multiplexer_4_out, not_1_out, not_2_out, sumador_flags_1_c, sumador_flags_1_v;
  wire [3:0] and_4_1_s, incrementador_4_1_s, inversor_4_1_s, multiplexer_1_out, multiplexer_2_out, or_4_1_s,
       sumador_flags_1_s;

  inversor_4 inversor_4_1 (.A(B), .INV(OP[0]), .S(inversor_4_1_s));
  AND_4 and_4_1 (.A(A), .B(B), .S(and_4_1_s));
  OR_4 or_4_1 (.A(A), .B(B), .S(or_4_1_s));
  incrementador_4 incrementador_4_1 (.A(inversor_4_1_s), .S(incrementador_4_1_s));
  Multiplexer #(.width(4)) multiplexer_1 (.in0(and_4_1_s), .in1(or_4_1_s), .out(multiplexer_1_out), .sel(OP[0]));
  Multiplexer #(.width(4)) multiplexer_2 (
    .in0(inversor_4_1_s), .in1(incrementador_4_1_s), .out(multiplexer_2_out), .sel(OP[0]));
  Hex_Digit_Display hex_digit_display_1 (.value(multiplexer_2_out));  // open: dp
  sumador_flags sumador_flags_1 (
    .a(A), .b(multiplexer_2_out), .S(sumador_flags_1_s), .V(sumador_flags_1_v), .N(N), .C(sumador_flags_1_c));  // open: cin, Z
  Multiplexer #(.width(4)) multiplexer_3 (.in0(multiplexer_1_out), .in1(sumador_flags_1_s), .out(S), .sel(not_1_out));
  not not_1 (not_1_out, OP[0]);
  not not_2 (not_2_out, sumador_flags_1_c);
  Multiplexer multiplexer_4 (.in0(sumador_flags_1_c), .in1(not_2_out), .out(multiplexer_4_out), .sel(OP[0]));
  Multiplexer multiplexer_5 (.in0(sumador_flags_1_v), .in1(1'b0), .out(V), .sel(OP[1]));
  Multiplexer multiplexer_6 (.in0(multiplexer_4_out), .in1(1'b0), .out(C), .sel(OP[1]));
  Hex_Digit_Display hex_digit_display_2 (.value(S));  // open: dp
  comparador_cero comparador_cero_1 (.A(S), .Z(Z));
endmodule

module comprobador_V (
  input  resta,
  input  [3:0] a,
  input  [3:0] b,
  output V
);

  wire multiplexer_2_out, not_1_out, xor_1_out, xor_2_out;
  wire [3:0] incrementador_4_1_s, inversor_4_1_s, multiplexer_1_out, sumador_4_1_s;

  inversor_4 inversor_4_1 (.A(b), .INV(resta), .S(inversor_4_1_s));
  incrementador_4 incrementador_4_1 (.A(inversor_4_1_s), .S(incrementador_4_1_s));
  xor xor_1 (xor_1_out, b[3], a[3]);
  Multiplexer #(.width(4)) multiplexer_1 (
    .in0(inversor_4_1_s), .in1(incrementador_4_1_s), .out(multiplexer_1_out), .sel(resta));
  sumador_4 sumador_4_1 (.A(a), .B(multiplexer_1_out), .S(sumador_4_1_s));  // open: Cin, Cout
  not not_1 (not_1_out, xor_1_out);
  Multiplexer multiplexer_2 (.in0(not_1_out), .in1(xor_1_out), .out(multiplexer_2_out), .sel(resta));
  xor xor_2 (xor_2_out, a[3], sumador_4_1_s[3]);
  and and_1 (V, multiplexer_2_out, xor_2_out);
endmodule
